# Fritzing sketch IOT_esp32 (saved by Fritzing 1.0.0d)
breadboards: 1

parts:
  U1 = ESP32-38PinWide [part_number=ESP32-38PinWide]
  HC-SR04_Sensor_1 = HC-SR04 Ultrasonic Distance Sensor
  WATER_PUMP1 = water pump/motor  # not connected
  Chirp!_Soil_Moisture_Sensor1 = Chirp! Soil Moisture Sensor v2.7.3
  DS1 = DS18B20 1-Wire Temperature Sensor [part_number=DS18B20]
  Q1 = TRANSISTOR_NPN [package=to-92]
  Part1 = Ambient Light Sensor (TEMT6000 Breakout Board)

nets:
  VCC: U1.3.3, HC-SR04_Sensor_1.VCC, Chirp!_Soil_Moisture_Sensor1.Pin_1, DS1.VDD, Part1.VCC
  N1: U1.GPIO34, Chirp!_Soil_Moisture_Sensor1.pin_3
  N2: U1.GPIO32, Part1.S
  N3: U1.GPIO33, DS1.DQ
  N4: U1.GPIO26, Q1.B
  N5: U1.GPIO12, HC-SR04_Sensor_1.TRIG
  GND: U1.GND, HC-SR04_Sensor_1.GND, Chirp!_Soil_Moisture_Sensor1.pin_5, DS1.GND, Q1.E, Part1.GND
  N6: U1.GPIO13, HC-SR04_Sensor_1.ECHO

custom parts:
  ESP32-38PinWide: Generic 38-Pin ESP32 with wide format (only access to one side of pins on a breadboard) based on Stephen Lilley's HiLetgo ESP-WROOM-32 ESP32 ESP-32S Development Board.
  water pump/motor: WATER PUMP BY ARDUBLOCKTR
